# Fritzing sketch WaterLevelController_mega (saved by Fritzing 0.9.2b)
breadboards: 1

parts:
  Part1 = Arduino Mega 2560 (Rev3)
  Part2 = Arduino Ethernet Shield (Rev3)
  U1 = 2-Channel 5v Relay Shield [package=relay-2ch5v10a]
  Part3 = SRF05 Ultrasonic Rangefinder
  Part4 = SRF05 Ultrasonic Rangefinder
  LCD2 = LCD screen

nets:
  N1: Part1.D22, Part3.Trig
  N2: Part1.D23, Part3.Echo
  N3: Part1.D24, Part4.Trig
  N4: Part1.D25, Part4.Echo
  N5: Part1.D26, U1.IN1, U1.IN2
  N6: Part1.D28, LCD2.RS
  N7: Part1.D29, LCD2.E
  N8: Part1.D30, LCD2.DB4
  N9: Part1.D31, LCD2.DB5
  N10: Part1.D32, LCD2.DB6
  N11: Part1.D33, LCD2.DB7
  VCC: Part2.5V, U1.VCC, Part3.VCC, Part4.VCC, LCD2.VDD, LCD2.LED-
  GND: Part2.GND, U1.GND, Part3.GND, Part4.GND, LCD2.VSS, LCD2.V0, LCD2.R/W, LCD2.DB0, LCD2.DB1, LCD2.DB2, LCD2.DB3, LCD2.LED+

custom parts:
  2-Channel 5v Relay Shield: 2 Channel 5v Relay Shield w. 2x SPD-06VDC-SD-C
  LCD screen: A standard character display, usually with 2x16 characters. Comes in many colors.
